// Digital circuit 2-Bit Multiplier.dig as structural Verilog
module _2_Bit_Multiplier (
  input  [1:0] A,
  input  [1:0] B,
  output [3:0] out_3
);

  wire and_1_out, and_2_out, and_4_out, and_5_out, and_6_out, and_7_out, and_8_out, and_9_out, and_11_out,
       not_1_out, not_2_out, not_3_out, not_4_out, not_5_out, or_1_out, or_2_out;

  and and_1 (and_1_out, A[1], B[0]);
  not not_1 (not_1_out, A[0]);
  and and_2 (and_2_out, A[0], B[1]);
  not not_2 (not_2_out, A[1]);
  and and_3 (out_3[0], A[0], B[0]);
  and and_4 (and_4_out, B[1], B[1]);
  not not_3 (not_3_out, B[0]);
  not not_4 (not_4_out, A[0]);
  not not_5 (not_5_out, B[1]);
  and and_5 (and_5_out, and_1_out, not_1_out);
  and and_6 (and_6_out, and_2_out, not_2_out);
  and and_7 (and_7_out, and_2_out, not_3_out);
  and and_8 (and_8_out, and_4_out, not_3_out);
  and and_9 (and_9_out, and_1_out, not_5_out);
  and and_10 (out_3[3], out_3[0], and_4_out);
  and and_11 (and_11_out, and_4_out, not_4_out);
  or or_1 (or_1_out, and_5_out, and_9_out);
  or or_2 (or_2_out, and_6_out, and_7_out);
  or or_3 (out_3[2], and_8_out, and_11_out);
  or or_4 (out_3[1], or_2_out, or_1_out);
endmodule
