// Digital circuit 4-bit-adder.dig as structural Verilog
module _4_bit_adder (
  input  [3:0] A,
  input  [3:0] B,
  output [3:0] Sum,
  output Overflow_flag
);

  wire _1_bit_adder_2_c_out, _1_bit_adder_3_c_out, _1_bit_adder_4_c_out;

  _1_bit_adder _1_bit_adder_1 (.A(A[3]), .B(B[3]), .C_in(_1_bit_adder_2_c_out), .Sum(Sum[3]), .C_out(Overflow_flag));
  _1_bit_adder _1_bit_adder_2 (
    .A(A[2]), .B(B[2]), .C_in(_1_bit_adder_3_c_out), .Sum(Sum[2]), .C_out(_1_bit_adder_2_c_out));
  _1_bit_adder _1_bit_adder_3 (
    .A(A[1]), .B(B[1]), .C_in(_1_bit_adder_4_c_out), .Sum(Sum[1]), .C_out(_1_bit_adder_3_c_out));
  _1_bit_adder _1_bit_adder_4 (.A(A[0]), .B(B[0]), .C_in(1'b0), .Sum(Sum[0]), .C_out(_1_bit_adder_4_c_out));
endmodule
